// Logisim project 1 to 8 Demultiplexer.circ as structural Verilog: 1 circuit, main circuit main
module main (
  input  S,
  input  S1,
  input  S2,
  input  I,
  output Y,
  output Y1,
  output Y2,
  output Y3,
  output Y4,
  output Y5,
  output Y6,
  output Y7
);

  wire not_1_out, not_2_out, not_3_out;

  not not_1 (not_1_out, S);
  not not_2 (not_2_out, S1);
  not not_3 (not_3_out, S2);
  and and_1 (Y, not_1_out, not_2_out, not_3_out, I);
  and and_2 (Y1, S, not_2_out, not_3_out, I);
  and and_3 (Y2, not_1_out, S1, not_3_out, I);
  and and_4 (Y3, S, S1, not_3_out, I);
  and and_5 (Y4, not_1_out, not_2_out, S2, I);
  and and_6 (Y5, S, not_2_out, S2, I);
  and and_7 (Y6, not_1_out, S1, S2, I);
  and and_8 (Y7, S, S1, S2, I);
endmodule
