// Logisim project 2 bit & 3 bit counter.circ as structural Verilog: 1 circuit, main circuit main
module main (
  input  in_1,
  input  in_2,
  output MSB,
  output LSB,
  output MSB_2,
  output out_6,
  output LSB_2
);

  wire and_1_out, clock_1_out, clock_2_out, not_1_out, not_2_out;

  Clock clock_1 (.out(clock_1_out));
  and and_1 (and_1_out, LSB_2, out_6);
  Clock clock_2 (.out(clock_2_out));
  T_Flip_Flop t_ff_1 (.clk(clock_1_out), .T(LSB), .Q(MSB));  // open: Qn, preset, reset, en
  T_Flip_Flop t_ff_2 (.clk(clock_2_out), .T(and_1_out), .Q(MSB_2));  // open: Qn, preset, reset, en
  not not_1 (not_1_out, in_1);
  T_Flip_Flop t_ff_3 (.clk(clock_1_out), .T(not_1_out), .Q(LSB));  // open: Qn, preset, reset, en
  T_Flip_Flop t_ff_4 (.clk(clock_2_out), .T(LSB_2), .Q(out_6));  // open: Qn, preset, reset, en
  not not_2 (not_2_out, in_2);
  T_Flip_Flop t_ff_5 (.clk(clock_2_out), .T(not_2_out), .Q(LSB_2));  // open: Qn, preset, reset, en

  // Notes on the sheet:
  //   2 bit counter
  //   3 bit counter
endmodule
