// Logisim project 8 to 1 Multiplexer.circ as structural Verilog: 1 circuit, main circuit main
module main (
  input  S,
  input  S1,
  input  S2,
  input  I,
  input  I1,
  input  I2,
  input  I3,
  input  I4,
  input  I5,
  input  I6,
  input  I7,
  input  E,
  output out_13
);

  wire and_1_out, and_2_out, and_3_out, and_4_out, and_5_out, and_6_out, and_7_out, and_8_out, not_1_out,
       not_2_out, not_3_out, not_4_out, not_5_out, not_6_out, not_7_out, not_8_out, not_9_out, not_10_out,
       not_11_out, or_1_out;

  not not_1 (not_1_out, S);
  not not_2 (not_2_out, S2);
  not not_3 (not_3_out, S1);
  not not_4 (not_4_out, I);
  not not_5 (not_5_out, I1);
  not not_6 (not_6_out, I2);
  not not_7 (not_7_out, I4);
  not not_8 (not_8_out, I3);
  not not_9 (not_9_out, I5);
  not not_10 (not_10_out, I6);
  not not_11 (not_11_out, I7);
  and and_1 (and_1_out, not_1_out, not_3_out, not_2_out, I);
  and and_2 (and_2_out, S, not_3_out, not_2_out, I1);
  and and_3 (and_3_out, not_1_out, S1, not_2_out, I2);
  and and_4 (and_4_out, S, S1, not_2_out, I3);
  and and_5 (and_5_out, not_1_out, not_3_out, S2, I4);
  and and_6 (and_6_out, S, not_3_out, S2, I5);
  and and_7 (and_7_out, not_1_out, S1, S2, I6);
  and and_8 (and_8_out, S, S1, S2, I7);
  or or_1 (or_1_out, and_1_out, and_2_out, and_3_out, and_4_out, and_5_out, and_6_out, and_7_out, and_8_out);
  and and_9 (out_13, or_1_out, E);

  // Notes on the sheet:
  //   Output
endmodule
