// Logisim project Binary to Gray conversion by NANDs and NORs.circ as structural Verilog: 1 circuit, main circuit main
module main (
  input  A,
  input  B,
  input  C,
  input  A_2,
  input  B_2,
  input  C_2,
  output D,
  output D_2,
  output E,
  output E_2,
  output F,
  output F_2
);

  wire nand_1_out, nand_2_out, nand_3_out, nand_4_out, nand_5_out, nand_6_out, nand_7_out, nor_1_out,
       nor_2_out, nor_3_out, nor_4_out, nor_5_out, nor_6_out, nor_7_out, nor_8_out, nor_9_out;

  nand nand_1 (nand_1_out, A, A);
  nand nand_2 (nand_2_out, B, B);
  nand nand_3 (nand_3_out, C, C);
  nand nand_4 (nand_4_out, nand_1_out, B);
  nand nand_5 (nand_5_out, A, nand_2_out);
  nand nand_6 (nand_6_out, nand_2_out, C);
  nand nand_7 (nand_7_out, nand_3_out, B);
  nand nand_8 (E, nand_4_out, nand_5_out);
  nand nand_9 (F, nand_6_out, nand_7_out);
  nor nor_1 (nor_1_out, A_2, A_2);
  nor nor_2 (nor_2_out, B_2, B_2);
  nor nor_3 (nor_3_out, C_2, C_2);
  nor nor_4 (nor_4_out, A_2, nor_2_out);
  nor nor_5 (nor_5_out, nor_1_out, B_2);
  nor nor_6 (nor_6_out, B_2, nor_3_out);
  nor nor_7 (nor_7_out, nor_2_out, C_2);
  nor nor_8 (nor_8_out, nor_4_out, nor_5_out);
  nor nor_9 (nor_9_out, nor_6_out, nor_7_out);
  nor nor_10 (E_2, nor_8_out, nor_8_out);
  nor nor_11 (F_2, nor_9_out, nor_9_out);

  assign D = A;
  assign D_2 = A_2;

  // Notes on the sheet:
  //   Binary to Gray with NANDs
  //   Binary to Gray with  NORs
endmodule
