// Logisim project Counter Design for a Given Sequence (2207034).circ as structural Verilog: 2 circuits, main circuit main
module main (
  input  in_1,
  output out_2,
  output out_3,
  output out_4
);

  wire and_1_out, and_2_out, and_3_out, and_4_out, clock_1_out, n7_segment_display_1_out_5,
       n7_segment_display_1_out_6, n7_segment_display_1_out_7, n7_segment_display_1_out_8,
       n7_segment_display_1_out_9, n7_segment_display_1_out_10, n7_segment_display_1_out_11, not_1_out,
       not_2_out, not_3_out, not_4_out, or_1_out, or_2_out, or_3_out, or_4_out, t_ff_1_q;

  Clock clock_1 (.out(clock_1_out));
  T_Flip_Flop t_ff_1 (.clk(clock_1_out), .T(or_4_out), .Q(t_ff_1_q));  // open: Qn, preset, reset, en
  not not_1 (not_1_out, t_ff_1_q);
  T_Flip_Flop t_ff_2 (.clk(clock_1_out), .T(or_3_out), .Q(out_2));  // open: Qn, preset, reset, en
  not not_2 (not_2_out, out_2);
  T_Flip_Flop t_ff_3 (.clk(clock_1_out), .T(or_2_out), .Q(out_3));  // open: Qn, preset, reset, en
  not not_3 (not_3_out, out_3);
  T_Flip_Flop t_ff_4 (.clk(clock_1_out), .T(or_1_out), .Q(out_4));  // open: Qn, preset, reset, en
  not not_4 (not_4_out, out_4);
  and and_1 (and_1_out, not_2_out, not_3_out);
  and and_2 (and_2_out, not_1_out, not_3_out);
  and and_3 (and_3_out, out_2, out_4);
  and and_4 (and_4_out, out_3, not_4_out);
  or or_1 (or_1_out, out_4, and_1_out);
  or or_2 (or_2_out, t_ff_1_q, not_3_out, out_4);
  or or_3 (or_3_out, out_4, and_2_out);
  or or_4 (or_4_out, t_ff_1_q, and_3_out, and_4_out);
  _7_Segment_Display u_7_segment_display_1 (
    .B(out_2), .C(out_3), .D(out_4), .in_4(in_1), .out_5(n7_segment_display_1_out_5),
    .out_6(n7_segment_display_1_out_6), .out_7(n7_segment_display_1_out_7),
    .out_8(n7_segment_display_1_out_8), .out_9(n7_segment_display_1_out_9),
    .out_10(n7_segment_display_1_out_10), .out_11(n7_segment_display_1_out_11));
  _7_Segment_Display_part u_7_segment_display_2 (
    .g(n7_segment_display_1_out_11), .f(n7_segment_display_1_out_10), .a(n7_segment_display_1_out_5),
    .b(n7_segment_display_1_out_6), .e(n7_segment_display_1_out_9), .d(n7_segment_display_1_out_8),
    .c(n7_segment_display_1_out_7));  // open: dp

  // Notes on the sheet:
  //   A
  //   B
  //   C
  //   D
endmodule

module _7_Segment_Display (
  input  B,
  input  C,
  input  D,
  input  in_4,
  output out_5,
  output out_6,
  output out_7,
  output out_8,
  output out_9,
  output out_10,
  output out_11
);

  wire not_3_out;

  not not_1 (out_8, B);
  not not_2 (out_10, C);
  not not_3 (not_3_out, D);
  or or_1 (out_5, out_8, C);
  not not_4 (out_6, in_4);
  or or_2 (out_7, out_10, D);
  and and_1 (out_9, out_8, not_3_out);
  xor xor_1 (out_11, B, C);
endmodule
