// Logisim project Full Substractor with NANDs and NORs.circ as structural Verilog: 1 circuit, main circuit main
module main (
  input  A,
  input  B,
  input  C,
  input  A_2,
  input  B_2,
  input  C_2,
  output out_7,
  output out_8,
  output out_9,
  output Borrow
);

  wire nand_1_out, nand_2_out, nand_3_out, nand_4_out, nand_5_out, nand_6_out, nand_7_out, nand_8_out,
       nand_9_out, nand_10_out, nor_1_out, nor_2_out, nor_3_out, nor_4_out, nor_5_out, nor_6_out, nor_7_out,
       nor_8_out, nor_9_out, nor_10_out, nor_11_out, nor_12_out;

  nand nand_1 (nand_1_out, A, A);
  nand nand_2 (nand_2_out, B, B);
  not nand_3 (nand_3_out, C);  // NAND_Gate
  nand nand_4 (nand_4_out, nand_1_out, nand_2_out, C);
  nand nand_5 (nand_5_out, nand_1_out, B, nand_3_out);
  nand nand_6 (nand_6_out, A, nand_2_out, nand_3_out);
  nand nand_7 (nand_7_out, A, B, C);
  nand nand_8 (nand_8_out, nand_1_out, B);
  nand nand_9 (nand_9_out, B, C);
  nand nand_10 (nand_10_out, C, nand_1_out);
  nand nand_11 (out_7, nand_4_out, nand_5_out, nand_6_out, nand_7_out);
  nand nand_12 (out_9, nand_8_out, nand_9_out, nand_10_out);
  nor nor_1 (nor_1_out, A_2, A_2);
  nor nor_2 (nor_2_out, B_2, B_2);
  nor nor_3 (nor_3_out, C_2, C_2);
  nor nor_4 (nor_4_out, A_2, B_2, nor_3_out);
  nor nor_5 (nor_5_out, A_2, nor_2_out, C_2);
  nor nor_6 (nor_6_out, nor_1_out, B_2, C_2);
  nor nor_7 (nor_7_out, nor_1_out, nor_2_out, nor_3_out);
  nor nor_8 (nor_8_out, A_2, nor_2_out);
  nor nor_9 (nor_9_out, nor_2_out, nor_3_out);
  nor nor_10 (nor_10_out, nor_3_out, A_2);
  nor nor_11 (nor_11_out, nor_4_out, nor_5_out, nor_6_out, nor_7_out);
  nor nor_12 (nor_12_out, nor_8_out, nor_9_out, nor_10_out);
  nor nor_13 (out_8, nor_11_out, nor_11_out);
  nor nor_14 (Borrow, nor_12_out, nor_12_out);

  // Notes on the sheet:
  //   With NAND Gates
  //   Borrow
  //   Difference
  //   With NOR Gates
  //   Difference
endmodule
