// Logisim project Gray to Binary conversion by NANDs and NORs.circ as structural Verilog: 1 circuit, main circuit main
module main (
  input  D,
  input  E,
  input  F,
  input  D_2,
  input  E_2,
  input  F_2,
  output A,
  output A_2,
  output B,
  output B_2,
  output C,
  output C_2
);

  wire nand_1_out, nand_2_out, nand_3_out, nand_4_out, nand_6_out, nand_7_out, nand_8_out, nand_10_out,
       nand_11_out, nor_1_out, nor_2_out, nor_3_out, nor_4_out, nor_5_out, nor_6_out, nor_7_out, nor_8_out,
       nor_9_out, nor_10_out, nor_13_out;

  nand nand_1 (nand_1_out, D, D);
  nand nand_2 (nand_2_out, E, E);
  nand nand_3 (nand_3_out, F, F);
  nand nand_4 (nand_4_out, nand_1_out, E);
  nand nand_5 (B, nand_4_out, nand_6_out);
  nand nand_6 (nand_6_out, D, nand_2_out);
  nand nand_7 (nand_7_out, nand_1_out, nand_2_out, F);
  nand nand_8 (nand_8_out, nand_1_out, E, nand_3_out);
  nand nand_9 (C, nand_7_out, nand_8_out, nand_10_out, nand_11_out);
  nand nand_10 (nand_10_out, D, nand_2_out, nand_3_out);
  nand nand_11 (nand_11_out, D, E, F);
  nor nor_1 (nor_1_out, D_2, D_2);
  nor nor_2 (nor_2_out, E_2, E_2);
  nor nor_3 (nor_3_out, F_2, F_2);
  nor nor_4 (nor_4_out, nor_1_out, E_2);
  nor nor_5 (nor_5_out, D_2, nor_2_out);
  nor nor_6 (nor_6_out, D_2, E_2, nor_3_out);
  nor nor_7 (nor_7_out, D_2, nor_2_out, F_2);
  nor nor_8 (nor_8_out, nor_1_out, E_2, F_2);
  nor nor_9 (nor_9_out, nor_1_out, nor_2_out, nor_3_out);
  nor nor_10 (nor_10_out, nor_4_out, nor_5_out);
  nor nor_11 (B_2, nor_10_out, nor_10_out);
  nor nor_12 (C_2, nor_13_out, nor_13_out);
  nor nor_13 (nor_13_out, nor_6_out, nor_7_out, nor_8_out, nor_9_out);

  assign A = D;
  assign A_2 = D_2;

  // Notes on the sheet:
  //   With NAND Gates
  //   With NOR Gates
endmodule
